# Fritzing sketch Sketch (saved by Fritzing 1.0.1rc)
breadboards: 2

parts:
  U1 = ESP32-38PinWide [part_number=ESP32-38PinWide]
  LCM1602_IIC1 = LCM1602 IIC [part_number="LCM1602 IIC" chip_label="LCM1602 IIC" package="DIP (Dual Inline) [THT]"]
  LCD1 = LCD screen

nets:
  GND: U1.GND, LCM1602_IIC1.GND
  VIN: U1.VIN, LCM1602_IIC1.VCC
  N1: U1.GPIO18, LCM1602_IIC1.SDA
  N2: U1.GPIO19, LCM1602_IIC1.SCL
  VSS: LCM1602_IIC1.VSS, LCD1.VSS
  VDD: LCM1602_IIC1.VDD, LCD1.VDD
  N3: LCM1602_IIC1.V0, LCD1.V0
  N4: LCM1602_IIC1.RS, LCD1.RS
  N5: LCM1602_IIC1.RW, LCD1.R/W
  N6: LCM1602_IIC1.E, LCD1.E
  N7: LCM1602_IIC1.D0, LCD1.DB0
  N8: LCM1602_IIC1.D1, LCD1.DB1
  N9: LCM1602_IIC1.D2, LCD1.DB2
  N10: LCM1602_IIC1.D3, LCD1.DB3
  N11: LCM1602_IIC1.D4, LCD1.DB4
  N12: LCM1602_IIC1.D5, LCD1.DB5
  N13: LCM1602_IIC1.D6, LCD1.DB6
  N14: LCM1602_IIC1.D7, LCD1.DB7
  N15: LCM1602_IIC1.A, LCD1.LED+
  N16: LCM1602_IIC1.K, LCD1.LED-

custom parts:
  ESP32-38PinWide: Generic 38-Pin ESP32 with wide format (only access to one side of pins on a breadboard) based on Stephen Lilley's HiLetgo ESP-WROOM-32 ESP32 ESP-32S Development Board.
  LCM1602 IIC: I2C-Module to use a 1602 or 2004 LCD on with the wire.h libory Serial LCD Modul
